// Logisim project LogiSim-IC 4511.circ as structural Verilog: 2 circuits, main circuit IC 4511
module IC_4511 (
  input  _8,
  input  _4,
  input  _2,
  input  _1,
  output out_5,
  output out_6,
  output out_7,
  output out_8,
  output out_9,
  output out_10,
  output out_11
);

  wire _0_out, _1_out, _2_out, _3_out, _4_out, _5_out, _7_out, _8_out, not_1_out, not_2_out, not_3_out,
       not_4_out;

  not not_1 (not_1_out, _8);
  not not_2 (not_2_out, _4);
  not not_3 (not_3_out, _2);
  not not_4 (not_4_out, _1);
  and _0 (_0_out, not_1_out, not_2_out, not_3_out, not_4_out);
  and u__1 (_1_out, _1, not_3_out, not_2_out, not_1_out);
  and u__2 (_2_out, _2, not_4_out, not_2_out, not_1_out);
  and _3 (_3_out, _1, _2, not_2_out, not_1_out);
  and u__4 (_4_out, _4, not_4_out, not_3_out, not_1_out);
  and _5 (_5_out, _4, _1, not_3_out, not_1_out);
  and _6 (_4_out, _4, _2, not_4_out, not_1_out);
  and _7 (_7_out, _4, _2, _1, not_1_out);
  and u__8 (_8_out, _8, not_4_out, not_3_out, not_2_out);
  and _9 (_4_out, _8, _1, not_3_out, not_2_out);
  or A (out_5, _0_out, _2_out, _3_out, _5_out, _4_out, _7_out, _8_out, _4_out);
  or B (out_6, _0_out, _1_out, _2_out, _3_out, _4_out, _7_out, _8_out, _4_out);
  or C (out_7, _0_out, _1_out, _3_out, _4_out, _5_out, _4_out, _7_out, _8_out, _4_out);
  or D (out_8, _0_out, _2_out, _3_out, _5_out, _4_out, _8_out, _4_out);
  or E (out_9, _0_out, _2_out, _4_out, _8_out);
  or F (out_10, _0_out, _4_out, _5_out, _4_out, _8_out, _4_out);
  or G (out_11, _2_out, _3_out, _4_out, _5_out, _4_out, _8_out, _4_out);
endmodule

module Test (
  input  in_1,
  input  in_2,
  input  in_3,
  input  in_4,
  output out_5,
  output out_6,
  output out_7,
  output out_8,
  output out_9,
  output out_10,
  output out_11
);

  IC_4511 IC_4511 (
    ._8(in_1), ._4(in_2), ._2(in_3), ._1(in_4), .out_5(out_5), .out_6(out_6), .out_7(out_7), .out_8(out_8),
    .out_9(out_9), .out_10(out_10), .out_11(out_11));
endmodule
